# Fritzing sketch ptz-joystick (saved by Fritzing 0.9.3b)
circuit board: 8.7cm x 6.6cm
breadboards: 1

parts:
  ADS1015 = Adafruit ADS1015 12Bit I2C ADC [part_number="Adafruit #1083"]
  Keypad = female pin header, 8 pins [form="♀ (female)"]
  I2C_bus = female pin header, 4 pins [form="♀ (female)"]
  I2C_bus1 = female pin header, 4 pins [form="♀ (female)"]
  I2C_bus2 = female pin header, 4 pins [form="♀ (female)"]
  I2C_bus3 = female pin header, 4 pins [form="♀ (female)"]
  LED5 = female pin header, 4 pins [form="♀ (female)"]
  LED4 = female pin header, 4 pins [form="♀ (female)"]
  LED3 = female pin header, 4 pins [form="♀ (female)"]
  LED2 = female pin header, 4 pins [form="♀ (female)"]
  LED1 = female pin header, 4 pins [form="♀ (female)"]
  LED6 = female pin header, 4 pins [form="♀ (female)"]
  LED7 = female pin header, 4 pins [form="♀ (female)"]
  LED8 = female pin header, 4 pins [form="♀ (female)"]
  LED9 = female pin header, 4 pins [form="♀ (female)"]
  LED10 = female pin header, 4 pins [form="♀ (female)"]
  LED11 = female pin header, 4 pins [form="♀ (female)"]
  LED12 = female pin header, 4 pins [form="♀ (female)"]
  LED13 = female pin header, 4 pins [form="♀ (female)"]
  LED14 = female pin header, 4 pins [form="♀ (female)"]
  LED15 = female pin header, 4 pins [form="♀ (female)"]
  LED16 = female pin header, 4 pins [form="♀ (female)"]
  Analog_input_1 = female pin header, 3 pins [form="♀ (female)"]
  Analog_input_2 = female pin header, 3 pins [form="♀ (female)"]
  Analog_input_3 = female pin header, 3 pins [form="♀ (female)"]
  Analog_input_4 = female pin header, 3 pins [form="♀ (female)"]
  RPi = mystery part, 40 pins [chip_label=?]
  5V = female pin header, 2 pins [form="♀ (female)"]
  Arcade_Joystic = female pin header, 5 pins [form="♀ (female)"]
  GND = female pin header, 2 pins [form="♀ (female)"]
  3v3 = female pin header, 2 pins [form="♀ (female)"]
  J2 = female pin header, 2 pins [form="♀ (female)"]
  AW9523 = mystery part, 22 pins [chip_label=?]
  J4 = female pin header, 2 pins [form="♀ (female)"]
  J3 = female pin header, 8 pins [form="♀ (female)"]
  J5 = female pin header, 2 pins [form="♀ (female)"]
  J6 = female pin header, 9 pins [form="♀ (female)"]

nets:
  N1: ADS1015.AIN3, Analog_input_1.pin3
  N2: ADS1015.AIN2, Analog_input_2.pin3
  N3: ADS1015.AIN1, Analog_input_3.pin3
  N4: ADS1015.AIN0, Analog_input_4.pin3
  N5: ADS1015.ALERT, J2.pin1
  N6: ADS1015.ADDR, J2.pin2
  N7: ADS1015.SDA, I2C_bus.pin4, I2C_bus1.pin4, I2C_bus2.pin4, I2C_bus3.pin4, RPi.pin2, AW9523.pin15
  N8: ADS1015.SCL, I2C_bus.pin3, I2C_bus1.pin3, I2C_bus2.pin3, I2C_bus3.pin3, RPi.pin3, AW9523.pin14
  N9: ADS1015.GND, Analog_input_1.pin1, Analog_input_2.pin1, Analog_input_3.pin1, Analog_input_4.pin1, RPi.pin13, J5.pin1
  N10: ADS1015.VDD, I2C_bus.pin1, I2C_bus1.pin1, I2C_bus2.pin1, I2C_bus3.pin1, LED5.pin3, LED4.pin3, LED3.pin3, LED2.pin3, LED1.pin3, LED6.pin3, LED7.pin3, LED8.pin3, LED9.pin3, LED10.pin3, LED11.pin3, LED12.pin3, LED13.pin3, LED14.pin3, LED15.pin3, LED16.pin3, Analog_input_1.pin2, Analog_input_2.pin2, Analog_input_3.pin2, Analog_input_4.pin2, RPi.pin1, 3v3.pin1, 3v3.pin2, AW9523.pin12
  N11: Keypad.pin1, RPi.pin4
  N12: Keypad.pin2, RPi.pin6
  N13: Keypad.pin3, RPi.pin7
  N14: Keypad.pin4, RPi.pin8
  N15: Keypad.pin5, RPi.pin10
  N16: Keypad.pin6, RPi.pin11
  N17: Keypad.pin7, RPi.pin12
  N18: I2C_bus.pin2, I2C_bus1.pin2, I2C_bus2.pin2, I2C_bus3.pin2, LED5.pin2, LED4.pin2, LED3.pin2, LED2.pin2, LED1.pin2, LED6.pin2, LED7.pin2, LED8.pin2, LED9.pin2, LED10.pin2, LED11.pin2, LED12.pin2, LED13.pin2, LED14.pin2, LED15.pin2, LED16.pin2, RPi.pin38, GND.pin1, GND.pin2
  N19: LED5.pin1, J6.pin5
  N20: LED5.pin4, AW9523.pin22
  N21: LED4.pin1, J6.pin4
  N22: LED4.pin4, AW9523.pin21
  N23: LED3.pin1, J6.pin3
  N24: LED3.pin4, AW9523.pin20
  N25: LED2.pin1, J6.pin2
  N26: LED2.pin4, AW9523.pin19
  N27: LED1.pin1, J6.pin1
  N28: LED1.pin4, AW9523.pin18
  N29: LED6.pin1, J6.pin6
  N30: LED6.pin4, AW9523.pin11
  N31: LED7.pin1, J6.pin7
  N32: LED7.pin4, AW9523.pin10
  N33: LED8.pin1, J6.pin8
  N34: LED8.pin4, AW9523.pin9
  N35: LED9.pin1, J6.pin9
  N36: LED9.pin4, AW9523.pin8
  N37: LED10.pin1, RPi.pin15
  N38: LED10.pin4, AW9523.pin7
  N39: LED11.pin1, RPi.pin16
  N40: LED11.pin4, AW9523.pin6
  N41: LED12.pin1, RPi.pin17
  N42: LED12.pin4, AW9523.pin5
  N43: LED13.pin1, RPi.pin18
  N44: LED13.pin4, AW9523.pin4
  N45: LED14.pin1, RPi.pin19
  N46: LED14.pin4, AW9523.pin3
  N47: LED15.pin1, RPi.pin21
  N48: LED15.pin4, AW9523.pin2
  N49: LED16.pin1, RPi.pin22
  N50: LED16.pin4, AW9523.pin1
  N51: RPi.pin14, J5.pin2
  N52: RPi.pin23, J3.pin8
  N53: RPi.pin24, J3.pin7
  N54: RPi.pin25, J3.pin6
  N55: RPi.pin26, J3.pin5
  N56: RPi.pin27, J3.pin4
  N57: RPi.pin28, J3.pin3
  N58: RPi.pin29, J3.pin2
  N59: RPi.pin30, J3.pin1
  N60: RPi.pin31, Arcade_Joystic.pin5, AW9523.pin13
  N61: RPi.pin33, Arcade_Joystic.pin4
  N62: RPi.pin35, Arcade_Joystic.pin3
  N63: RPi.pin36, Arcade_Joystic.pin2
  N64: RPi.pin37, Arcade_Joystic.pin1
  N65: RPi.pin39, 5V.pin1, 5V.pin2
  N66: AW9523.pin16, J4.pin1
  N67: AW9523.pin17, J4.pin2

notes:
  I2C bus
  Vcc
  GND
  SCL
  SDA
  3v3
  5v
  Ain
  ptz-joystick
  v1.1
  8
  10
  9
  11
  15
  0
  14
  12
  13
  7
  5
  6
  4
  2
  3
  1
  RST
  INT
  ADDR
  ALERT
  Arcade Joystick
  Left
  Up
  Right
  Down
  Mounting holes 80x60mm M2
  Board 87x66mm

custom parts:
  Adafruit ADS1015 12Bit I2C ADC: For microcontrollers without an analog-to-digital converter or when you want a higher-precision ADC, the ADS1015 provides 12-bit precision at 3300 samples/second over I2C. The chip can be configured as 4 single-ended input channels, or two differential channels. As a nice bonus, it even includes a programmable gain amplifier, up to x16, to help boost up smaller single/differential signals to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
